# Fritzing sketch HitagiExpansionBoard (saved by Fritzing 0.9.5d)
circuit board: 10.5cm x 13.5033cm
breadboards: 1

parts:
  MCP23S17 = MCP23S17 [part_number=MCP23S17 package="DIP (Dual Inline) [THT]"]
  C1 = Ceramic Capacitor [capacitance=0.1µF voltage=50V package="0805 [SMD, multilayer]"]
  Contrast = TRIMPOT [package=trimpot-3mm]
  SparkFun_Pro_Micro_5v = SparkFun Pro Micro [part_number=DEV-12640]
  STEMMA = female pin header, 4 pins [form="♀ (female)"]
  RESET = Pushbutton [package="[THT]"]
  BAT1 = BC9VPC [package=bc9vpc]
  POWER = Toggle Switch [package=THT]
  23LC1024 = 23LCV1024 [part_number=23LC1024 package="DIP (Dual Inline) [THT]"]
  STEMMA1 = Adafruit Stemma 4 pin header [form="♀ (female)" package=THT]
  STEMMA2 = Adafruit Stemma 4 pin header [form="♀ (female)" package=THT]
  R7 = Resistor [tolerance=±5% resistance=10k package="0805 [SMD]"]
  R5 = Resistor [tolerance=±5% resistance=10k package="0805 [SMD]"]
  R6 = Resistor [tolerance=±5% resistance=10k package="0805 [SMD]"]
  STEMMA3 = Adafruit Stemma 4 pin header [form="♀ (female)" package=THT]
  PWM(5) = female pin header, 3 pins [form="♀ (female)"]
  SPI0 = JST PH SPI HEADER [form="♀ (female)" package=THT]
  SPI1 = JST PH SPI HEADER [form="♀ (female)" package=THT]
  SPI2 = JST PH SPI HEADER [form="♀ (female)" package=THT]
  D7 = female pin header, 3 pins [form="♀ (female)"]
  C2 = Ceramic Capacitor [capacitance=0.1µF voltage=50V package="0805 [SMD, multilayer]"]
  LCD = Adafruit Positive RGB 2x16 LCD
  SPI3 = JST PH SPI HEADER [form="♀ (female)" package=THT]

nets:
  P7: MCP23S17.GPB0
  P6: MCP23S17.GPB1
  P5: MCP23S17.GPB2
  P4: MCP23S17.GPB3
  P3: MCP23S17.GPB4
  P2: MCP23S17.GPB5
  P1: MCP23S17.GPB6
  P0: MCP23S17.GPB7
  23LC1024 VCC/5V/MCP23S17_VCC: MCP23S17.VDD, C1.1, Contrast.CW, SparkFun_Pro_Micro_5v.VCC, STEMMA.pin2, 23LC1024.VCC, STEMMA1.V+, STEMMA2.V+, R7.Pin_0, R5.Pin_0, R6.Pin_0, STEMMA3.V+, PWM(5).pin2, SPI0.VCC, SPI1.VCC, SPI2.VCC, D7.pin2, C2.1, LCD.no_name_yet#1, LCD.no_name_yet#14, LCD.no_name_yet#101, LCD.no_name_yet#114, SPI3.VCC
  23LC1024 GND/GND/MCP23S17_GND: MCP23S17.VSS, MCP23S17.A0, MCP23S17.A1, MCP23S17.A2, C1.0, Contrast.CCW, SparkFun_Pro_Micro_5v.GND, STEMMA.pin1, RESET.Pin_3, RESET.Pin_4, BAT1.V-, 23LC1024.VSS, STEMMA1.GND, STEMMA2.GND, STEMMA3.GND, PWM(5).pin1, SPI0.GND, SPI1.GND, SPI2.GND, D7.pin1, C2.0, LCD.no_name_yet#0, LCD.no_name_yet#100, SPI3.GND
  MCP23S17 ENABLE: MCP23S17.CS_, SparkFun_Pro_Micro_5v.A1
  SCK: MCP23S17.SCK, SparkFun_Pro_Micro_5v.SCK, 23LC1024.SCK, SPI0.SCK, SPI1.SCK, SPI2.SCK, SPI3.SCK
  MOSI: MCP23S17.SI, SparkFun_Pro_Micro_5v.MOSI, 23LC1024.SI/SIO0, SPI0.MOSI, SPI1.MOSI, SPI2.MOSI, SPI3.MOSI
  MISO: MCP23S17.SO, SparkFun_Pro_Micro_5v.MISO, 23LC1024.SO/SIO1, SPI0.MISO, SPI1.MISO, SPI2.MISO, SPI3.MISO
  RESET: MCP23S17.RESET_, SparkFun_Pro_Micro_5v.RESET, RESET.Pin_1, RESET.Pin_2
  P8: MCP23S17.GPA0
  RS: MCP23S17.GPA1, LCD.no_name_yet#3, LCD.no_name_yet#103
  RW: MCP23S17.GPA2, LCD.no_name_yet#4, LCD.no_name_yet#104
  E: MCP23S17.GPA3, LCD.no_name_yet#5, LCD.no_name_yet#105
  A4: MCP23S17.GPA4, LCD.no_name_yet#10, LCD.no_name_yet#110
  A5: MCP23S17.GPA5, LCD.no_name_yet#11, LCD.no_name_yet#111
  A6: MCP23S17.GPA6, LCD.no_name_yet#12, LCD.no_name_yet#112
  A7: MCP23S17.GPA7, LCD.no_name_yet#13, LCD.no_name_yet#113
  CONTRAST: Contrast.WIPER, LCD.no_name_yet#2, LCD.no_name_yet#102
  9V: SparkFun_Pro_Micro_5v.RAW, POWER.COM
  SPI3 Enable: SparkFun_Pro_Micro_5v.A3, SPI3.CS_
  SPI2 Enable: SparkFun_Pro_Micro_5v.A2, SPI2.CS_
  SRAM Enable: SparkFun_Pro_Micro_5v.A0, 23LC1024.CS_, R7.Pin_1
  RED PWM: SparkFun_Pro_Micro_5v.D10, LCD.no_name_yet#15, LCD.no_name_yet#115
  BLUE PWM: SparkFun_Pro_Micro_5v.D9, LCD.no_name_yet#17, LCD.no_name_yet#117
  SPI1 Enable: SparkFun_Pro_Micro_5v.D8, SPI1.CS_
  D7: SparkFun_Pro_Micro_5v.D7, D7.pin3
  GREEN PWM: SparkFun_Pro_Micro_5v.D6, LCD.no_name_yet#16, LCD.no_name_yet#116
  PWM0: SparkFun_Pro_Micro_5v.D5, PWM(5).pin3
  SPI0 Enable: SparkFun_Pro_Micro_5v.D4, SPI0.CS_
  SCL: SparkFun_Pro_Micro_5v.D3, STEMMA.pin4, STEMMA1.SCL, STEMMA2.SCL, STEMMA3.SCL
  SDA: SparkFun_Pro_Micro_5v.D2, STEMMA.pin3, STEMMA1.SDA, STEMMA2.SDA, STEMMA3.SDA
  9V IN: BAT1.V+, POWER.L1
  N1: 23LC1024.NC, R5.Pin_1
  N2: 23LC1024.VBAT, R6.Pin_1

notes:
  REV 2
  "Hitagi" Expansion Board
  (C) 2020 Joshua Scoggins

custom parts:
  MCP23S17: 28-pin DIP Package version of the MCP23S17 16-bit I/O Expander with SPI Interface
  SparkFun Pro Micro: This tiny little board does all of the neat-o Arduino tricks that you’re familiar with: 4 channels of 10-bit ADC, 5 PWM pins, 12 DIOs as well as hardware serial connections Rx and Tx. Running at 16MHz and 5V, this board will remind you a lot of your other favorite Arduino-compatible boards but this little guy can go just about anywhere. There is a voltage regulator on board so it can accept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
  Adafruit Stemma 4 pin header: Adafruit STEMMA 4 pin header JST PH 4
  JST PH SPI HEADER: Single device JST PH Based SPI Header
  Adafruit Positive RGB 2x16 LCD: Adafruit Positive 2x16 LCD Display with RGB Backlight
